# Fritzing sketch Solar Charge Board production1 (saved by Fritzing 0.9.1b)
circuit board: 10.4cm x 11.7cm
breadboards: 1

parts:
  C1 = Ceramic Capacitor [capacitance="100 nF" part_number="Kemet # C1206C104K5RAC" package="1206 [SMD, multilayer]"]
  C2 = Ceramic Capacitor [capacitance="100 nF" part_number="Kemet # C1206C104K5RAC" package="1206 [SMD, multilayer]"]
  C3 = Ceramic Capacitor [capacitance="100 nF" part_number="Kemet # C1206C104K5RAC" package="1206 [SMD, multilayer]"]
  C4 = Ceramic Capacitor [capacitance="100 nF" part_number="Kemet # C1206C104K5RAC" package="1206 [SMD, multilayer]"]
  C5 = Ceramic Capacitor [capacitance="100 nF" part_number="Kemet # C1206C104K5RAC" package="1206 [SMD, multilayer]"]
  C8 = Ceramic Capacitor [capacitance="100 nF" part_number="Kemet # C1206C104K5RAC" package="1206 [SMD, multilayer]"]
  C6 = Ceramic Capacitor [capacitance="100 nF" part_number="Kemet # C1206C104K5RAC" package="1206 [SMD, multilayer]"]
  C10 = Ceramic Capacitor [capacitance="100 nF" part_number="Kemet # C1206C104K5RAC" package="1206 [SMD, multilayer]"]
  C9 = Ceramic Capacitor [capacitance="100 nF" part_number="Kemet # C1206C104K5RAC" package="1206 [SMD, multilayer]"]
  C7 = Ceramic Capacitor [capacitance="100 nF" part_number="Kemet # C1206C104K5RAC" package="1206 [SMD, multilayer]"]
  C13 = Ceramic Capacitor [capacitance="100 nF" part_number="Kemet # C1206C104K5RAC" package="1206 [SMD, multilayer]"]
  C18 = Ceramic Capacitor [capacitance="100 nF" part_number="Kemet # C1206C104K5RAC" package="1206 [SMD, multilayer]"]
  C11 = Ceramic Capacitor [capacitance="100 nF" part_number="Kemet # C1206C104K5RAC" package="1206 [SMD, multilayer]"]
  C16 = Ceramic Capacitor [capacitance="100 nF" part_number="Kemet # C1206C104K5RAC" package="1206 [SMD, multilayer]"]
  C15 = Ceramic Capacitor [capacitance="100 nF" part_number="Kemet # C1206C104K5RAC" package="1206 [SMD, multilayer]"]
  C20 = Ceramic Capacitor [capacitance="100 nF" part_number="Kemet # C1206C104K5RAC" package="1206 [SMD, multilayer]"]
  C14 = Ceramic Capacitor [capacitance="100 nF" part_number="Kemet # C1206C104K5RAC" package="1206 [SMD, multilayer]"]
  C19 = Ceramic Capacitor [capacitance="100 nF" part_number="Kemet # C1206C104K5RAC" package="1206 [SMD, multilayer]"]
  C17 = Ceramic Capacitor [capacitance="100 nF" part_number="Kemet # C1206C104K5RAC" package="1206 [SMD, multilayer]"]
  C12 = Ceramic Capacitor [capacitance="100 nF" part_number="Kemet # C1206C104K5RAC" package="1206 [SMD, multilayer]"]
  C28 = Ceramic Capacitor [capacitance="100 nF" part_number="Kemet # C1206C104K5RAC" package="1206 [SMD, multilayer]"]
  C33 = Ceramic Capacitor [capacitance="100 nF" part_number="Kemet # C1206C104K5RAC" package="1206 [SMD, multilayer]"]
  C38 = Ceramic Capacitor [capacitance="100 nF" part_number="Kemet # C1206C104K5RAC" package="1206 [SMD, multilayer]"]
  C23 = Ceramic Capacitor [capacitance="100 nF" part_number="Kemet # C1206C104K5RAC" package="1206 [SMD, multilayer]"]
  C21 = Ceramic Capacitor [capacitance="100 nF" part_number="Kemet # C1206C104K5RAC" package="1206 [SMD, multilayer]"]
  C31 = Ceramic Capacitor [capacitance="100 nF" part_number="Kemet # C1206C104K5RAC" package="1206 [SMD, multilayer]"]
  C36 = Ceramic Capacitor [capacitance="100 nF" part_number="Kemet # C1206C104K5RAC" package="1206 [SMD, multilayer]"]
  C26 = Ceramic Capacitor [capacitance="100 nF" part_number="Kemet # C1206C104K5RAC" package="1206 [SMD, multilayer]"]
  C25 = Ceramic Capacitor [capacitance="100 nF" part_number="Kemet # C1206C104K5RAC" package="1206 [SMD, multilayer]"]
  C35 = Ceramic Capacitor [capacitance="100 nF" part_number="Kemet # C1206C104K5RAC" package="1206 [SMD, multilayer]"]
  C40 = Ceramic Capacitor [capacitance="100 nF" part_number="Kemet # C1206C104K5RAC" package="1206 [SMD, multilayer]"]
  C30 = Ceramic Capacitor [capacitance="100 nF" part_number="Kemet # C1206C104K5RAC" package="1206 [SMD, multilayer]"]
  C24 = Ceramic Capacitor [capacitance="100 nF" part_number="Kemet # C1206C104K5RAC" package="1206 [SMD, multilayer]"]
  C29 = Ceramic Capacitor [capacitance="100 nF" part_number="Kemet # C1206C104K5RAC" package="1206 [SMD, multilayer]"]
  C39 = Ceramic Capacitor [capacitance="100 nF" part_number="Kemet # C1206C104K5RAC" package="1206 [SMD, multilayer]"]
  C34 = Ceramic Capacitor [capacitance="100 nF" part_number="Kemet # C1206C104K5RAC" package="1206 [SMD, multilayer]"]
  C37 = Ceramic Capacitor [capacitance="100 nF" part_number="Kemet # C1206C104K5RAC" package="1206 [SMD, multilayer]"]
  C32 = Ceramic Capacitor [capacitance="100 nF" part_number="Kemet # C1206C104K5RAC" package="1206 [SMD, multilayer]"]
  C22 = Ceramic Capacitor [capacitance="100 nF" part_number="Kemet # C1206C104K5RAC" package="1206 [SMD, multilayer]"]
  C27 = Ceramic Capacitor [capacitance="100 nF" part_number="Kemet # C1206C104K5RAC" package="1206 [SMD, multilayer]"]
  C43 = Ceramic Capacitor [capacitance="100 nF" part_number="Kemet # C1206C104K5RAC" package="1206 [SMD, multilayer]"]
  C41 = Ceramic Capacitor [capacitance="100 nF" part_number="Kemet # C1206C104K5RAC" package="1206 [SMD, multilayer]"]
  C45 = Ceramic Capacitor [capacitance="100 nF" part_number="Kemet # C1206C104K5RAC" package="1206 [SMD, multilayer]"]
  C44 = Ceramic Capacitor [capacitance="100 nF" part_number="Kemet # C1206C104K5RAC" package="1206 [SMD, multilayer]"]
  C42 = Ceramic Capacitor [capacitance="100 nF" part_number="Kemet # C1206C104K5RAC" package="1206 [SMD, multilayer]"]
  Arduino_Nano = Arduino Nano (Rev3.0)
  C48 = Ceramic Capacitor [capacitance="100 nF" part_number="Kemet # C1206C104K5RAC" package="1206 [SMD, multilayer]"]
  C46 = Ceramic Capacitor [capacitance="100 nF" part_number="Kemet # C1206C104K5RAC" package="1206 [SMD, multilayer]"]
  C50 = Ceramic Capacitor [capacitance="100 nF" part_number="Kemet # C1206C104K5RAC" package="1206 [SMD, multilayer]"]
  C49 = Ceramic Capacitor [capacitance="100 nF" part_number="Kemet # C1206C104K5RAC" package="1206 [SMD, multilayer]"]
  C47 = Ceramic Capacitor [capacitance="100 nF" part_number="Kemet # C1206C104K5RAC" package="1206 [SMD, multilayer]"]
  C53 = Ceramic Capacitor [capacitance="100 nF" part_number="Kemet # C1206C104K5RAC" package="1206 [SMD, multilayer]"]
  C51 = Ceramic Capacitor [capacitance="100 nF" part_number="Kemet # C1206C104K5RAC" package="1206 [SMD, multilayer]"]
  C52 = Ceramic Capacitor [capacitance="100 nF" part_number="Kemet # C1206C104K5RAC" package="1206 [SMD, multilayer]"]
  C58 = Ceramic Capacitor [capacitance="100 nF" part_number="Kemet # C1206C104K5RAC" package="1206 [SMD, multilayer]"]
  C57 = Ceramic Capacitor [capacitance="100 nF" part_number="Kemet # C1206C104K5RAC" package="1206 [SMD, multilayer]"]
  C56 = Ceramic Capacitor [capacitance="100 nF" part_number="Kemet # C1206C104K5RAC" package="1206 [SMD, multilayer]"]
  C54 = Ceramic Capacitor [capacitance="100 nF" part_number="Kemet # C1206C104K5RAC" package="1206 [SMD, multilayer]"]
  C55 = Ceramic Capacitor [capacitance="100 nF" part_number="Kemet # C1206C104K5RAC" package="1206 [SMD, multilayer]"]
  J2 = female pin header, 9 pins [form="♀ (female)"]
  J3 = female pin header, 3 pins [form="♀ (female)"]
  F1 = Resettable Fuse PTC [part_number="Digi-Key 490-3973-ND" package=ptc]
  R1 = Resistor [tolerance=±5% resistance=100 package="0603 [SMD]"]
  LED1 = smd LED [color="Blue (525nm)" current=20mA package="0805 [SMD]"]
  RGB24 = SMD RGB LED (WS2812B) [package=5050]
  RGB14 = SMD RGB LED (WS2812B) [package=5050]
  RGB15 = SMD RGB LED (WS2812B) [package=5050]
  RGB26 = SMD RGB LED (WS2812B) [package=5050]
  RGB07 = SMD RGB LED (WS2812B) [package=5050]
  RGB08 = SMD RGB LED (WS2812B) [package=5050]
  RGB13 = SMD RGB LED (WS2812B) [package=5050]
  RGB49 = SMD RGB LED (WS2812B) [package=5050]
  RGB52 = SMD RGB LED (WS2812B) [package=5050]
  RGB04 = SMD RGB LED (WS2812B) [package=5050]
  RGB03 = SMD RGB LED (WS2812B) [package=5050]
  RGB25 = SMD RGB LED (WS2812B) [package=5050]
  RGB31 = SMD RGB LED (WS2812B) [package=5050]
  RGB39 = SMD RGB LED (WS2812B) [package=5050]
  RGB43 = SMD RGB LED (WS2812B) [package=5050]
  RGB48 = SMD RGB LED (WS2812B) [package=5050]
  RGB51 = SMD RGB LED (WS2812B) [package=5050]
  RGB58 = SMD RGB LED (WS2812B) [package=5050]
  RGB23 = SMD RGB LED (WS2812B) [package=5050]
  RGB38 = SMD RGB LED (WS2812B) [package=5050]
  RGB17 = SMD RGB LED (WS2812B) [package=5050]
  RGB02 = SMD RGB LED (WS2812B) [package=5050]
  RGB42 = SMD RGB LED (WS2812B) [package=5050]
  RGB16 = SMD RGB LED (WS2812B) [package=5050]
  RGB10 = SMD RGB LED (WS2812B) [package=5050]
  RGB35 = SMD RGB LED (WS2812B) [package=5050]
  RGB32 = SMD RGB LED (WS2812B) [package=5050]
  RGB09 = SMD RGB LED (WS2812B) [package=5050]
  RGB06 = SMD RGB LED (WS2812B) [package=5050]
  RGB19 = SMD RGB LED (WS2812B) [package=5050]
  RGB34 = SMD RGB LED (WS2812B) [package=5050]
  RGB20 = SMD RGB LED (WS2812B) [package=5050]
  RGB29 = SMD RGB LED (WS2812B) [package=5050]
  RGB36 = SMD RGB LED (WS2812B) [package=5050]
  RGB21 = SMD RGB LED (WS2812B) [package=5050]
  RGB44 = SMD RGB LED (WS2812B) [package=5050]
  RGB45 = SMD RGB LED (WS2812B) [package=5050]
  RGB53 = SMD RGB LED (WS2812B) [package=5050]
  RGB18 = SMD RGB LED (WS2812B) [package=5050]
  RGB55 = SMD RGB LED (WS2812B) [package=5050]
  RGB54 = SMD RGB LED (WS2812B) [package=5050]
  RGB50 = SMD RGB LED (WS2812B) [package=5050]
  RGB05 = SMD RGB LED (WS2812B) [package=5050]
  RGB30 = SMD RGB LED (WS2812B) [package=5050]
  RGB37 = SMD RGB LED (WS2812B) [package=5050]
  RGB33 = SMD RGB LED (WS2812B) [package=5050]
  RGB11 = SMD RGB LED (WS2812B) [package=5050]
  RGB28 = SMD RGB LED (WS2812B) [package=5050]
  RGB22 = SMD RGB LED (WS2812B) [package=5050]
  RGB01 = SMD RGB LED (WS2812B) [package=5050]
  RGB12 = SMD RGB LED (WS2812B) [package=5050]
  RGB47 = SMD RGB LED (WS2812B) [package=5050]
  RGB46 = SMD RGB LED (WS2812B) [package=5050]
  RGB57 = SMD RGB LED (WS2812B) [package=5050]
  RGB56 = SMD RGB LED (WS2812B) [package=5050]
  RGB40 = SMD RGB LED (WS2812B) [package=5050]
  RGB27 = SMD RGB LED (WS2812B) [package=5050]
  RGB41 = SMD RGB LED (WS2812B) [package=5050]
  J1 = XT60 Connector [package=THT]

nets:
  GND: C1.0, C2.0, C3.0, C4.0, C5.0, C8.0, C6.0, C10.0, C9.0, C7.0, C13.0, C18.0, C11.0, C16.0, C15.0, C20.0, C14.0, C19.0, C17.0, C12.0, C28.0, C33.0, C38.0, C23.0, C21.0, C31.0, C36.0, C26.0, C25.0, C35.0, C40.0, C30.0, C24.0, C29.0, C39.0, C34.0, C37.0, C32.0, C22.0, C27.0, C43.0, C41.0, C45.0, C44.0, C42.0, Arduino_Nano.GND, C48.0, C46.0, C50.0, C49.0, C47.0, C53.0, C51.0, C52.0, C58.0, C57.0, C56.0, C54.0, C55.0, J3.pin3, LED1.cathode, RGB24.VSS, RGB14.VSS, RGB15.VSS, RGB26.VSS, RGB07.VSS, RGB08.VSS, RGB13.VSS, RGB49.VSS, RGB52.VSS, RGB04.VSS, RGB03.VSS, RGB25.VSS, RGB31.VSS, RGB39.VSS, RGB43.VSS, RGB48.VSS, RGB51.VSS, RGB58.VSS, RGB23.VSS, RGB38.VSS, RGB17.VSS, RGB02.VSS, RGB42.VSS, RGB16.VSS, RGB10.VSS, RGB35.VSS, RGB32.VSS, RGB09.VSS, RGB06.VSS, RGB19.VSS, RGB34.VSS, RGB20.VSS, RGB29.VSS, RGB36.VSS, RGB21.VSS, RGB44.VSS, RGB45.VSS, RGB53.VSS, RGB18.VSS, RGB55.VSS, RGB54.VSS, RGB50.VSS, RGB05.VSS, RGB30.VSS, RGB37.VSS, RGB33.VSS, RGB11.VSS, RGB28.VSS, RGB22.VSS, RGB01.VSS, RGB12.VSS, RGB47.VSS, RGB46.VSS, RGB57.VSS, RGB56.VSS, RGB40.VSS, RGB27.VSS, RGB41.VSS, J1.GND
  5V: C1.1, C2.1, C3.1, C4.1, C5.1, C8.1, C6.1, C10.1, C9.1, C7.1, C13.1, C18.1, C11.1, C16.1, C15.1, C20.1, C14.1, C19.1, C17.1, C12.1, C28.1, C33.1, C38.1, C23.1, C21.1, C31.1, C36.1, C26.1, C25.1, C35.1, C40.1, C30.1, C24.1, C29.1, C39.1, C34.1, C37.1, C32.1, C22.1, C27.1, C43.1, C41.1, C45.1, C44.1, C42.1, Arduino_Nano.VIN, C48.1, C46.1, C50.1, C49.1, C47.1, C53.1, C51.1, C52.1, C58.1, C57.1, C56.1, C54.1, C55.1, F1.2, R1.Pin_1, RGB24.VDD, RGB14.VDD, RGB15.VDD, RGB26.VDD, RGB07.VDD, RGB08.VDD, RGB13.VDD, RGB49.VDD, RGB52.VDD, RGB04.VDD, RGB03.VDD, RGB25.VDD, RGB31.VDD, RGB39.VDD, RGB43.VDD, RGB48.VDD, RGB51.VDD, RGB58.VDD, RGB23.VDD, RGB38.VDD, RGB17.VDD, RGB02.VDD, RGB42.VDD, RGB16.VDD, RGB10.VDD, RGB35.VDD, RGB32.VDD, RGB09.VDD, RGB06.VDD, RGB19.VDD, RGB34.VDD, RGB20.VDD, RGB29.VDD, RGB36.VDD, RGB21.VDD, RGB44.VDD, RGB45.VDD, RGB53.VDD, RGB18.VDD, RGB55.VDD, RGB54.VDD, RGB50.VDD, RGB05.VDD, RGB30.VDD, RGB37.VDD, RGB33.VDD, RGB11.VDD, RGB28.VDD, RGB22.VDD, RGB01.VDD, RGB12.VDD, RGB47.VDD, RGB46.VDD, RGB57.VDD, RGB56.VDD, RGB40.VDD, RGB27.VDD, RGB41.VDD
  N1: Arduino_Nano.D1/TX, J3.pin1
  N2: Arduino_Nano.D0/RX, J3.pin2
  N3: Arduino_Nano.D2, RGB01.DIN
  N4: Arduino_Nano.D3, RGB06.DIN
  N5: Arduino_Nano.D4, RGB11.DIN
  N6: Arduino_Nano.D5, RGB16.DIN
  N7: Arduino_Nano.D6, RGB21.DIN
  N8: Arduino_Nano.D7, RGB26.DIN
  N9: Arduino_Nano.D8, RGB31.DIN
  N10: Arduino_Nano.D9, RGB36.DIN
  N11: Arduino_Nano.D10, RGB41.DIN
  N12: Arduino_Nano.D11/MOSI, RGB46.DIN
  N13: Arduino_Nano.D12/MISO, RGB54.DIN
  N14: Arduino_Nano.A7, J2.pin1
  N15: Arduino_Nano.A6, J2.pin2
  N16: Arduino_Nano.A5, J2.pin3
  N17: Arduino_Nano.A4, J2.pin4
  N18: Arduino_Nano.A3, J2.pin5
  N19: Arduino_Nano.A2, J2.pin6
  N20: Arduino_Nano.A1, J2.pin7
  N21: Arduino_Nano.A0, J2.pin8
  N22: Arduino_Nano.D13/SCK, J2.pin9
  N23: F1.1, J1.VCC
  N24: R1.Pin_0, LED1.anode
  N25: RGB24.DOUT, RGB25.DIN
  N26: RGB24.DIN, RGB23.DOUT
  N27: RGB14.DOUT, RGB15.DIN
  N28: RGB14.DIN, RGB13.DOUT
  N29: RGB26.DOUT, RGB27.DIN
  N30: RGB07.DOUT, RGB08.DIN
  N31: RGB07.DIN, RGB06.DOUT
  N32: RGB08.DOUT, RGB09.DIN
  N33: RGB13.DIN, RGB12.DOUT
  N34: RGB49.DOUT, RGB50.DIN
  N35: RGB49.DIN, RGB48.DOUT
  N36: RGB52.DOUT, RGB53.DIN
  N37: RGB52.DIN, RGB51.DOUT
  N38: RGB04.DOUT, RGB05.DIN
  N39: RGB04.DIN, RGB03.DOUT
  N40: RGB03.DIN, RGB02.DOUT
  N41: RGB31.DOUT, RGB32.DIN
  N42: RGB39.DOUT, RGB40.DIN
  N43: RGB39.DIN, RGB38.DOUT
  N44: RGB43.DOUT, RGB44.DIN
  N45: RGB43.DIN, RGB42.DOUT
  N46: RGB48.DIN, RGB47.DOUT
  N47: RGB51.DIN, RGB50.DOUT
  N48: RGB58.DIN, RGB57.DOUT
  N49: RGB23.DIN, RGB22.DOUT
  N50: RGB38.DIN, RGB37.DOUT
  N51: RGB17.DOUT, RGB18.DIN
  N52: RGB17.DIN, RGB16.DOUT
  N53: RGB02.DIN, RGB01.DOUT
  N54: RGB42.DIN, RGB41.DOUT
  N55: RGB10.DIN, RGB09.DOUT
  N56: RGB35.DIN, RGB34.DOUT
  N57: RGB32.DOUT, RGB33.DIN
  N58: RGB19.DOUT, RGB20.DIN
  N59: RGB19.DIN, RGB18.DOUT
  N60: RGB34.DIN, RGB33.DOUT
  N61: RGB29.DOUT, RGB30.DIN
  N62: RGB29.DIN, RGB28.DOUT
  N63: RGB36.DOUT, RGB37.DIN
  N64: RGB21.DOUT, RGB22.DIN
  N65: RGB44.DOUT, RGB45.DIN
  N66: RGB55.DOUT, RGB56.DIN
  N67: RGB55.DIN, RGB54.DOUT
  N68: RGB11.DOUT, RGB12.DIN
  N69: RGB28.DIN, RGB27.DOUT
  N70: RGB47.DIN, RGB46.DOUT
  N71: RGB57.DIN, RGB56.DOUT

notes:
  TX RX GND
  A7 thru A0   / D13
  Nano USB
  5V
  3A
  https://github.com/vemeT5ak
  Wall-E Solar Charge Panel rev1

custom parts:
  SMD RGB LED (WS2812B): The WS2812B is an RGB LED with a WS2811 control IC built right into the LED. Its improvement over its WS2812 ancestor is the reduction to 4 pins (a single power supply instead of 2) and dropping the requirement for the external resistors. The manufacturer says it has a better reverse connect protection.
  XT60 Connector: Yellow XT60 connector for high current loads up to 40A
